# Fritzing sketch Fritzing (saved by Fritzing 0.7.12b)
breadboards: 1

parts:
  T1 = LM35 Temperature Sensor [package="TO92 [THT]"]
  R2 = Resistor [tolerance=±5% resistance=220 package=THT]
  RTC1 = DS1307 RTC Breakout
  S1 = Pushbutton [package="[THT]"]
  POT1 = Breadboard Trimpot
  R1 = Resistor [tolerance=±5% resistance=10k package=THT]
  Arduino1 = Arduino
  LCD1 = LCD screen

nets:
  N1: T1.+Vs, Arduino1.aref, Arduino1.3V3
  N2: T1.Vout, Arduino1.A1
  GND: T1.GND, RTC1.GND, POT1.PIN1, R1.Pin_1, Arduino1.GND, LCD1.VSS, LCD1.R/W, LCD1.LED-
  5V: R2.Pin_0, RTC1.5V, S1.Pin_1, S1.Pin_2, POT1.PIN3, Arduino1.+5V, LCD1.VDD
  N3: R2.Pin_1, LCD1.LED+
  N4: RTC1.SDA, Arduino1.SDA
  N5: RTC1.SCL, Arduino1.SCL
  N6: S1.Pin_3, S1.Pin_4, R1.Pin_0, Arduino1.D10
  N7: POT1.PIN2, LCD1.V0
  N8: Arduino1.D9, LCD1.RS
  N9: Arduino1.D8, LCD1.E
  N10: Arduino1.D5, LCD1.DB4
  N11: Arduino1.D4, LCD1.DB5
  N12: Arduino1.D3, LCD1.DB6
  N13: Arduino1.D2, LCD1.DB7

custom parts:
  DS1307 RTC Breakout: DS1307 Real-time Clock Breakout Board with Battery
